# Fritzing sketch Treppenlicht (saved by Fritzing 0.9.2b)
stripboards: 2
perfboards: 1

parts:
  IC1 = IC, DIP package, 28 pins [chip_label=PIC32MX150F128B]
  D1 = Rectifier Diode [part_number=1N4001 package="300 mil [THT]"]
  U1 = Voltage Regulator - Variable [part_number=LM317 package="TO220 [THT]"]
  C1 = Electrolytic Capacitor [capacitance=100µF package="100 mil [THT, electrolytic]"]
  C2 = Ceramic Capacitor [capacitance=100nF package="100 mil [THT, multilayer]"]
  R3 = Resistor [tolerance=±5% resistance=1k package=THT]
  R4 = Resistor [tolerance=±5% resistance=1.6k package=THT]
  C4 = Electrolytic Capacitor [capacitance=100µF package="100 mil [THT, electrolytic]"]
  R5 = Resistor [tolerance=±5% resistance=10k package=THT]
  C5 = Ceramic Capacitor [capacitance=100nF package="100 mil [THT, multilayer]"]
  J1 = male pin header, 5 pins [form="♂ (male)"]
  C6 = Ceramic Capacitor [capacitance=100nF package="100 mil [THT, multilayer]"]
  C7 = Ceramic Capacitor [capacitance=100nF package="100 mil [THT, multilayer]"]
  J2 = Screw terminal - 2 pins [package=THT]
  R6 = Resistor [tolerance=±5% resistance=180 package=THT]
  J4 = female pin header, 1 pin [form="♀ (female)"]
  Q1 = Basic FET N-Channel [part_number=IRLZ34N package="TO220 [THT]"]
  R7 = Resistor [tolerance=±5% resistance=10k package=THT]

nets:
  Reset: IC1.pin1, R5.Pin_1, J1.pin1
  3.3V: IC1.pin2, IC1.pin13, IC1.pin28, U1.OUT, R3.Pin_0, C4.+, R5.Pin_0, J1.pin2, C6.1, C7.0
  GND: IC1.pin3, IC1.pin8, IC1.pin19, IC1.pin27, C1.-, C2.0, R4.Pin_1, C4.-, C5.0, J1.pin3, C6.0, C7.1, J2.pin2, Q1.source, R7.Pin_1
  N1: IC1.pin4, J1.pin4
  N2: IC1.pin5, J1.pin5
  SDA: IC1.pin16
  SCL: IC1.pin17
  N3: IC1.pin20, C5.1
  LED1: IC1.pin26, R6.Pin_0
  12V: D1.cathode, U1.IN, C1.+, C2.1
  N4: D1.anode, J2.pin1
  N5: U1.ADJ, R3.Pin_1, R4.Pin_0
  N6: R6.Pin_1, Q1.gate, R7.Pin_0
  N7: J4.pin1, Q1.drain
